# Fritzing sketch drinking-buddy-vibrator (saved by Fritzing 0.9.3b)
breadboards: 1

parts:
  WeMos_D1_Mini1 = WeMos D1 Mini
  U1 = Vibration Motor- ROB-08449 [part_number=vibe-motor package=vibe-motor-10mm]
  R1 = Resistor [tolerance=±5% resistance=272 package=THT]
  D1 = Rectifier Diode [part_number=1N4007 package="300 mil [THT]"]  # not connected
  Q1 = NPN-Transistor [part_number=2N2222 package="TO92 [THT]"]

nets:
  N1: WeMos_D1_Mini1.3V3, U1.-
  N2: WeMos_D1_Mini1.D0, R1.Pin_1
  N3: WeMos_D1_Mini1.G, Q1.C
  N4: U1.+, Q1.E
  N5: R1.Pin_0, Q1.B
